// Logisim project muxrisccore.circ as structural Verilog: 1 circuit, main circuit main
module main (
);

  wire clock_1_out, clock_2_out, clock_3_out, clock_4_out, clock_5_out, clock_6_out, clock_7_out,
       comparator_1_eq, comparator_2_eq, comparator_3_eq, comparator_4_eq, comparator_5_eq, comparator_5_gt,
       comparator_6_eq, comparator_6_gt, comparator_7_eq, comparator_7_gt, counter_1_q, counter_2_q,
       counter_3_q, multiplexer_3_out, or_1_out, or_2_out, or_3_out, or_4_out;
  wire [1:0] bitselector_1_out;
  wire [15:0] bitselector_2_out, counter_4_q, multiplexer_2_out, undriven;
  wire [63:0] multiplexer_1_out, multiplexer_4_out, ram_1_dout, register_1_q, register_2_q;

  Register #(.trigger("falling"), .width(64)) register_1 (
    .D(multiplexer_1_out), .en(1'b1), .clk(clock_1_out), .Q(register_1_q));  // open: clr
  Multiplexer #(.width(64)) multiplexer_1 (.in0(ram_1_dout), .in1({64{1'b0}}), .out(multiplexer_1_out), .sel(or_4_out));
  Clock clock_1 (.out(clock_1_out));
  BitSelector #(.group(2), .width(64)) bitselector_1 (.in(register_1_q), .out(bitselector_1_out), .sel({5{1'b0}}));
  Comparator #(.width(2)) comparator_1 (.a(bitselector_1_out), .b(2'b00), .eq(comparator_1_eq));  // open: gt, lt
  Comparator #(.width(2)) comparator_2 (.a(bitselector_1_out), .b(2'b01), .eq(comparator_2_eq));  // open: gt, lt
  Clock clock_2 (.out(clock_2_out));
  Comparator #(.width(2)) comparator_3 (.a(bitselector_1_out), .b(2'b10), .eq(comparator_3_eq));  // open: gt, lt
  Clock clock_3 (.out(clock_3_out));
  Comparator #(.width(2)) comparator_4 (.a(bitselector_1_out), .b(2'b11), .eq(comparator_4_eq));  // open: gt, lt
  Clock clock_4 (.out(clock_4_out));
  or or_1 (or_1_out, comparator_5_gt, comparator_5_eq);
  Counter #(.max('h1), .width(1)) counter_1 (
    .count(comparator_2_eq), .Q(counter_1_q), .clk(clock_2_out), .clr(comparator_1_eq));  // open: load, D, carry, up
  Comparator #(.mode("unsigned"), .width(1)) comparator_5 (
    .a(counter_1_q), .b(1'b1), .gt(comparator_5_gt), .eq(comparator_5_eq));  // open: lt
  or or_2 (or_2_out, comparator_6_gt, comparator_6_eq);
  Counter #(.max('h1), .width(1)) counter_2 (
    .count(comparator_3_eq), .Q(counter_2_q), .clk(clock_3_out), .clr(comparator_1_eq));  // open: load, D, carry, up
  Comparator #(.mode("unsigned"), .width(1)) comparator_6 (
    .a(counter_2_q), .b(1'b1), .gt(comparator_6_gt), .eq(comparator_6_eq));  // open: lt
  or or_3 (or_3_out, comparator_7_gt, comparator_7_eq);
  Counter #(.max('h1), .width(1)) counter_3 (
    .count(comparator_4_eq), .Q(counter_3_q), .clk(clock_4_out), .clr(comparator_1_eq));  // open: load, D, carry, up
  Comparator #(.mode("unsigned"), .width(1)) comparator_7 (
    .a(counter_3_q), .b(1'b1), .gt(comparator_7_gt), .eq(comparator_7_eq));  // open: lt
  or or_4 (or_4_out, or_1_out, or_2_out, or_3_out);
  BitSelector #(.group(16), .width(64)) bitselector_2 (.in(ram_1_dout), .out(bitselector_2_out), .sel(2'b00));
  Clock clock_5 (.out(clock_5_out));
  Register #(.width(64)) register_2 (
    .D(ram_1_dout), .en(comparator_3_eq), .clk(clock_6_out), .Q(register_2_q));  // open: clr
  Clock clock_6 (.out(clock_6_out));
  Counter #(.max('hffff), .trigger("falling"), .width(16)) counter_4 (
    .load(or_1_out), .D(bitselector_2_out), .Q(counter_4_q), .clk(clock_5_out));  // open: count, carry, up, clr
  Multiplexer #(.select(2), .width(16)) multiplexer_2 (
    .in0(counter_4_q), .in1(counter_4_q), .in2(counter_4_q), .in3(undriven), .out(multiplexer_2_out),
    .sel(bitselector_1_out));
  Clock clock_7 (.out(clock_7_out));
  Multiplexer #(.select(2)) multiplexer_3 (
    .in0(1'b0), .in1(1'b0), .in2(1'b0), .in3(or_3_out), .out(multiplexer_3_out), .sel(bitselector_1_out));
  Multiplexer #(.select(2), .width(64)) multiplexer_4 (
    .in0({64{1'b0}}), .in1({64{1'b0}}), .in2({64{1'b0}}), .in3(register_2_q), .out(multiplexer_4_out),
    .sel(bitselector_1_out));
  RAM #(.addrWidth(16), .dataWidth(64), .enables("line"), .\type ("nonvolatile")) ram_1 (
    .addr(multiplexer_2_out), .we(multiplexer_3_out), .clk(clock_7_out), .din(multiplexer_4_out),
    .dout(ram_1_dout));
endmodule
